# Fritzing sketch IR (saved by Fritzing 0.9.0b)
circuit board: 1.63571cm x 1.0316cm
breadboards: 1

parts:
  J1 = female pin header, 3 pins [form="♀ (female)"]
  R1 = Resistor [tolerance=±5% resistance=220 package=THT]
  LED1 = LED - 5mm [color="Infrared (940nm)" package="5 mm [THT]"]
  LED2 = LED - 5mm [color="Infrared (940nm)" package="5 mm [THT]"]
  R2 = Resistor [tolerance=±5% resistance=10k package=THT]

nets:
  N1: J1.pin1, R1.Pin_1, R2.Pin_1
  N2: J1.pin2, LED1.cathode, R2.Pin_0
  N3: J1.pin3, LED1.anode, LED2.anode
  N4: R1.Pin_0, LED2.cathode

notes:
  + S -
  220
  10K
