# Fritzing sketch Bluetooth (saved by Fritzing 0.9.0b)
circuit board: 1.34956cm x 0.925205cm
breadboards: 1

parts:
  J1 = female pin header, 4 pins [form="♀ (female)"]
  J2 = female pin header, 4 pins [form="♀ (female)"]
  R1 = Resistor [tolerance=±5% resistance=470k package=THT]
  R2 = Resistor [tolerance=±5% resistance=330k package=THT]

nets:
  N1: J1.pin1, J2.pin1
  N2: J1.pin2, J2.pin2, R1.Pin_1
  N3: J1.pin3, J2.pin3
  N4: J1.pin4, R1.Pin_0, R2.Pin_0
  N5: J2.pin4, R2.Pin_1

notes:
  RX TX - +
  TX RX - +
